// Digital circuit mcpu16.dig as structural Verilog
module mcpu16 (
  input  clock,
  input  [15:0] dIn,
  output wr,
  output [13:0] Addr,
  output [15:0] dOut
);

  wire add_2_c_o, and_1_out, C, d_ff_1_q, hA, hC, hCI, hE, limpC, not_3_out, register_1_q, register_2_q, sULA;
  wire [13:0] add_1_s, CI_q, multiplexer_1_out;
  wire [15:0] add_2_s, multiplexer_2_out, nor_1_out;

  Add #(.Bits(14)) add_1 (.a(Addr), .b({14{1'b0}}), .c_i(1'b1), .s(add_1_s));  // open: c_o
  Register #(.Bits(14)) CI (.D(add_1_s), .C(clock), .en(hCI), .Q(CI_q));
  assign nor_1_out = ~(dIn | dOut);  // NOr nor_1, 16 bits wide
  Register register_1 (.D(dIn[14]), .C(clock), .en(hCI), .Q(register_1_q));
  Register register_2 (.D(dIn[15]), .C(clock), .en(hCI), .Q(register_2_q));
  D_FF d_ff_1 (.D(hCI), .C(clock), .Q(d_ff_1_q), .nQ(hCI));
  Add #(.Bits(16)) add_2 (.a(dIn), .b(dOut), .c_i(1'b0), .s(add_2_s), .c_o(add_2_c_o));
  Multiplexer #(.Bits(14)) multiplexer_1 (.sel(hCI), .in_0(CI_q), .in_1(dIn[13:0]), .out(multiplexer_1_out));
  and and_1 (and_1_out, limpC, add_2_c_o);
  not not_1 (sULA, register_1_q);
  not not_2 (limpC, register_2_q);
  Multiplexer #(.Bits(16)) multiplexer_2 (.sel(sULA), .in_0(add_2_s), .in_1(nor_1_out), .out(multiplexer_2_out));
  Register #(.Bits(14)) E (.D(multiplexer_1_out), .C(clock), .en(hE), .Q(Addr));
  Register u_C (.D(and_1_out), .C(clock), .en(hC), .Q(C));
  Register #(.Bits(16)) A (.D(multiplexer_2_out), .C(clock), .en(hA), .Q(dOut));
  not not_3 (not_3_out, C);
  and and_2 (hC, register_1_q, d_ff_1_q);
  and and_3 (hA, d_ff_1_q, limpC);
  and and_4 (wr, d_ff_1_q, register_2_q, sULA);
  nand nand_1 (hE, d_ff_1_q, register_1_q, register_2_q, not_3_out);

  // Other names for the same wires on the sheet: d14 = dIn[14]; d15 = dIn[15]; grava = wr; sE = hCI

  // Notes on the sheet:
  //   clock: Hz: 2147483647
  //   wr: indicates a write to memory
endmodule
