// Digital circuit mcpu16_term.dig as structural Verilog
module mcpu16_term (
  input  relogio
);

  wire add_2_c_o, and_1_out, and_5_out, and_6_out, C, comparator_1_eq, d14, d15, d_ff_1_q, grava, hA, hC,
       hCI, hE, limpC, not_3_out, register_1_q, register_2_q, sULA;
  wire [13:0] add_1_s, CI_q, E_q, multiplexer_1_out, multiplexer_3_out;
  wire [15:0] A_q, add_2_s, keyboard_1_d, multiplexer_2_out, nor_1_out, ramdualport_1_d;

  Add #(.Bits(14)) add_1 (.a(E_q), .b({14{1'b0}}), .c_i(1'b1), .s(add_1_s));  // open: c_o
  Register #(.Bits(14)) CI (.D(add_1_s), .C(relogio), .en(hCI), .Q(CI_q));
  assign nor_1_out = ~({d15, d14, multiplexer_3_out} | A_q);  // NOr nor_1, 16 bits wide
  Register register_1 (.D(d14), .C(relogio), .en(hCI), .Q(register_1_q));
  Register register_2 (.D(d15), .C(relogio), .en(hCI), .Q(register_2_q));
  D_FF d_ff_1 (.D(hCI), .C(relogio), .Q(d_ff_1_q), .nQ(hCI));
  Add #(.Bits(16)) add_2 (.a({d15, d14, multiplexer_3_out}), .b(A_q), .c_i(1'b0), .s(add_2_s), .c_o(add_2_c_o));
  Multiplexer #(.Bits(14)) multiplexer_1 (.sel(hCI), .in_0(CI_q), .in_1(multiplexer_3_out), .out(multiplexer_1_out));
  and and_1 (and_1_out, limpC, add_2_c_o);
  not not_1 (sULA, register_1_q);
  not not_2 (limpC, register_2_q);
  Multiplexer #(.Bits(16)) multiplexer_2 (.sel(sULA), .in_0(add_2_s), .in_1(nor_1_out), .out(multiplexer_2_out));
  Register #(.Bits(14)) E (.D(multiplexer_1_out), .C(relogio), .en(hE), .Q(E_q));
  Register u_C (.D(and_1_out), .C(relogio), .en(hC), .Q(C));
  Register #(.Bits(16)) A (.D(multiplexer_2_out), .C(relogio), .en(hA), .Q(A_q));
  not not_3 (not_3_out, C);
  and and_2 (hC, register_1_q, d_ff_1_q);
  and and_3 (hA, d_ff_1_q, limpC);
  and and_4 (grava, d_ff_1_q, register_2_q, sULA);
  nand nand_1 (hE, d_ff_1_q, register_1_q, register_2_q, not_3_out);
  Comparator #(.Bits(14)) comparator_1 (.a(E_q), .b({14{1'b1}}), .eq(comparator_1_eq));  // open: gt, lt
  RAMDualPort #(.AddrBits(14), .isProgramMemory("true"), .Bits(16)) ramdualport_1 (
    .A(E_q), .Din(A_q), .str(grava), .C(relogio), .ld(1'b1), .D(ramdualport_1_d));
  and and_5 (and_5_out, ~grava, comparator_1_eq);  // And
  and and_6 (and_6_out, comparator_1_eq, grava);
  Keyboard keyboard_1 (.C(relogio), .en(and_5_out), .D(keyboard_1_d));  // open: av
  Terminal terminal_1 (.D(A_q), .C(relogio), .en(and_6_out));
  Multiplexer #(.Bits(16)) multiplexer_3 (
    .sel(comparator_1_eq), .in_0(ramdualport_1_d), .in_1(keyboard_1_d), .out({d15, d14, multiplexer_3_out}));

  // Other names for the same wires on the sheet: sE = hCI

  // Notes on the sheet:
  //   relogio: Hz: 2147483647
endmodule
