// Digital circuit mcpu16mc.dig as structural Verilog
// single cycle version of a 16 bit MCPU. It has 4 instructions:
// - NOR
// - ADD
// - STA
// - JCC
module mcpu16mc (
  input  [15:0] Instr,
  input  [15:0] Din,
  input  clock,
  output [13:0] PC,
  output [13:0] Addr,
  output [15:0] Dout,
  output wr
);

  wire add_1_c_o, and_1_out, and_2_out, Carry_q, not_1_out, not_2_out, not_3_out;
  wire [13:0] add_2_s, multiplexer_2_out;
  wire [15:0] add_1_s, multiplexer_1_out, nor_1_out;

  assign nor_1_out = ~(Din | Dout);  // NOr nor_1, 16 bits wide
  Add #(.Bits(16)) add_1 (.a(Din), .b(Dout), .c_i(1'b0), .s(add_1_s), .c_o(add_1_c_o));
  Add #(.Bits(14)) add_2 (.a(PC), .b({14{1'b0}}), .c_i(1'b1), .s(add_2_s));  // open: c_o
  not not_1 (not_1_out, Instr[15]);
  and and_1 (and_1_out, not_1_out, add_1_c_o);
  Multiplexer #(.Bits(16)) multiplexer_1 (.sel(Instr[14]), .in_0(nor_1_out), .in_1(add_1_s), .out(multiplexer_1_out));
  Multiplexer #(.Bits(14)) multiplexer_2 (.sel(and_2_out), .in_0(add_2_s), .in_1(Instr[13:0]), .out(multiplexer_2_out));
  not not_2 (not_2_out, Instr[14]);
  Register Carry (.D(and_1_out), .C(clock), .en(Instr[14]), .Q(Carry_q));
  Register #(.Bits(16)) Accumulator (.D(multiplexer_1_out), .C(clock), .en(not_1_out), .Q(Dout));
  and and_2 (and_2_out, Instr[14], Instr[15], not_3_out);
  not not_3 (not_3_out, Carry_q);
  D_FF #(.Bits(14)) u_PC (.D(multiplexer_2_out), .C(clock), .Q(PC));  // open: nQ
  and and_3 (wr, not_2_out, Instr[15]);

  assign Addr = Instr[13:0];

  // Notes on the sheet:
  //   PC: selects the instruction
  //   Instr: Data from instruction memory
  //   Addr: select word from data memory
  //   Din: word from data memory
  //   clock: Hz: 50000
  //   Dout: data for the data memory
  //   wr: write to data memory
endmodule
