// Digital circuit termcnt.dig as structural Verilog
// Terminal and Counter
// read 0xFFFFFFFE - clear counter
// write 0xFFFFFFFE - output current count
// read 0xFFFFFFFF - keyboard
// write 0xFFFFFFFF - output to terminal
module termcnt (
  input  relogio,
  input  write,
  input  read,
  input  [31:0] Addr,
  input  [15:0] dMemOut,
  input  [15:0] dIn,
  output [15:0] dOut,
  output [31:0] cnt
);

  wire and_1_out, and_2_out, and_3_out, and_4_out, comparator_1_eq, not_1_out;
  wire [15:0] keyboard_1_d;
  wire [31:0] counter_1_out;

  not not_1 (not_1_out, Addr[0]);
  Comparator #(.Bits(31)) comparator_1 (.a(Addr[31:1]), .b({31{1'b1}}), .eq(comparator_1_eq));  // open: gt, lt
  and and_1 (and_1_out, comparator_1_eq, Addr[0], write);
  and and_2 (and_2_out, comparator_1_eq, Addr[0], read);
  and and_3 (and_3_out, comparator_1_eq, not_1_out, read);
  and and_4 (and_4_out, comparator_1_eq, not_1_out, write);
  Counter #(.Bits(32)) counter_1 (.en(1'b1), .C(relogio), .clr(and_3_out), .out(counter_1_out));  // open: ovf
  Keyboard keyboard_1 (.C(relogio), .en(and_2_out), .D(keyboard_1_d));  // open: av
  Terminal terminal_1 (.D(dIn), .C(relogio), .en(and_1_out));
  Register #(.Bits(32)) register_1 (.D(counter_1_out), .C(relogio), .en(and_4_out), .Q(cnt));
  Multiplexer #(.Bits(16)) multiplexer_1 (.sel(comparator_1_eq), .in_0(dMemOut), .in_1(keyboard_1_d), .out(dOut));

  // Notes on the sheet:
  //   relogio: Hz: 2147483647
  //   write: indicates that the processor's data should be saved
  //   dOut: data to processor
  //   read: indicates processor expects data
  //   dMemOut: data from memory
  //   dIn: data from processor
  //   cnt: number of clock cycles counted
endmodule
