// Digital circuit alu_test.dig as structural Verilog
module alu_test (
  input  [3:0] op,
  input  [7:0] A,
  input  [7:0] B,
  input  clk,
  output [7:0] R,
  output Z,
  output C
);

  wire add_1_c_o, multiplexer_1_out, nand_1_out, nor_1_out;
  wire [7:0] add_1_s, and_1_out, and_2_out, multiplexer_2_out, or_1_out, xor_1_out, xor_2_out;

  assign or_1_out = A | B;  // Or or_1, 8 bits wide
  assign xor_1_out = A ^ B;  // XOr xor_1, 8 bits wide
  assign and_1_out = A & B;  // And and_1, 8 bits wide
  assign and_2_out = A & {8{op[1]}};  // And and_2, 8 bits wide
  assign xor_2_out = B ^ {8{op[0]}};  // XOr xor_2, 8 bits wide
  Multiplexer #(.Selector_Bits(2)) multiplexer_1 (
    .sel(op[3:2]), .in_0(1'b0), .in_1(1'b1), .in_2(C), .in_3(C), .out(multiplexer_1_out));
  Add #(.Bits(8)) add_1 (.a(and_2_out), .b(xor_2_out), .c_i(multiplexer_1_out), .s(add_1_s), .c_o(add_1_c_o));
  nand nand_1 (nand_1_out, op[3], op[2]);
  Multiplexer #(.Bits(8), .Selector_Bits(2)) multiplexer_2 (
    .sel(op[1:0]), .in_0(or_1_out), .in_1(xor_1_out), .in_2(and_1_out), .in_3(A), .out(multiplexer_2_out));
  Register register_1 (.D(nor_1_out), .C(clk), .en(nand_1_out), .Q(Z));
  Register register_2 (.D(add_1_c_o), .C(clk), .en(nand_1_out), .Q(C));
  nor nor_1 (nor_1_out, R[0], R[1], R[2], R[3], R[4], R[5], R[6], R[7]);
  Multiplexer #(.Bits(8)) multiplexer_3 (.sel(nand_1_out), .in_0(multiplexer_2_out), .in_1(add_1_s), .out(R));
endmodule

/* Test case test0:
op A B R

loop(a,256)
  loop(b,256)
    0 (a) (b) (b)
  end loop
end loop
*/

/* Test case test1:
op A B R

loop(a,256)
  loop(b,256)
    1 (a) (b) (~b)
  end loop
end loop
*/

/* Test case test2:
op A B R

loop(a,256)
  loop(b,256)
    2 (a) (b) (a+b)
  end loop
end loop
*/

/* Test case test3:
op A B R

loop(a,256)
  loop(b,256)
    3 (a) (b) (a-b-1)
  end loop
end loop
*/

/* Test case test4:
op A B R

loop(a,256)
  loop(b,256)
    4 (a) (b) (b+1)
  end loop
end loop
*/

/* Test case test5:
op A B R

loop(a,256)
  loop(b,256)
    5 (a) (b) (-b)
  end loop
end loop
*/

/* Test case test6:
op A B R

loop(a,256)
  loop(b,256)
    6 (a) (b) (a+b+1)
  end loop
end loop
*/

/* Test case test7:
op A B R

loop(a,256)
  loop(b,256)
    7 (a) (b) (a-b)
  end loop
end loop
*/

/* Test case test8:
op A B R

loop(a,256)
  loop(b,256)
    8 (a) (b) (b)
  end loop
end loop
*/

/* Test case test9:
op A B R

loop(a,256)
  loop(b,256)
    9 (a) (b) (~b)
  end loop
end loop
*/

/* Test case test10:
op A B R

loop(a,256)
  loop(b,256)
    10 (a) (b) (a+b)
  end loop
end loop
*/

/* Test case test11:
op A B R

loop(a,256)
  loop(b,256)
   11 (a) (b) (a-b-1)
  end loop
end loop
*/

/* Test case test12:
op A B R

loop(a,256)
  loop(b,256)
    12 (a) (b) (a|b)
  end loop
end loop
*/

/* Test case test13:
op A B R

loop(a,256)
  loop(b,256)
    13 (a) (b) (a^b)
  end loop
end loop
*/

/* Test case test14:
op A B R

loop(a,256)
  loop(b,256)
    14 (a) (b) (a&b)
  end loop
end loop
*/

/* Test case test15:
op A B R

loop(a,256)
  loop(b,256)
    15 (a) (b) (a)
  end loop
end loop
*/
