// Digital circuit ncpu_terminal.dig as structural Verilog
module ncpu_terminal (
  input  clock
);

  wire and_1_out, and_2_out, and_4_out, and_6_out, and_7_out, and_8_out, and_11_out, and_13_out, and_14_out,
       and_15_out, and_16_out, C, eF, eI, ePC, eR0, eR1, eR2, fetch_nq, multiplexer_2_out, or_1_out,
       or_3_out, skip_nq, skip_q, wr, xnor_1_out, Z;
  wire [1:0] multiplexer_1_out, multiplexer_1_out_2, sA, sB;
  wire [3:0] multiplexer_3_out, offset, op;
  wire [7:0] alu_1_r, instr, multiplexer_7_out, multiplexer_8_out, PC_q, r0_q, r1_q, r2_q, ramdualport_1_d;

  and and_1 (and_1_out, ~and_6_out, fetch_nq);  // And
  D_FF skip (.D(and_6_out), .C(clock), .Q(skip_q), .nQ(skip_nq));
  D_FF fetch (.D(and_1_out), .C(clock), .Q(eI), .nQ(fetch_nq));
  and and_2 (and_2_out, ~and_8_out, and_4_out);  // And
  and and_3 (eR0, ~multiplexer_1_out[0], ~multiplexer_1_out[1], and_2_out);  // And
  Multiplexer #(.Bits(8)) multiplexer_1 (
    .sel(or_1_out), .in_0(instr), .in_1(8'h34), .out({multiplexer_1_out_2, multiplexer_1_out, offset}));
  or or_1 (or_1_out, skip_q, eI);
  and and_4 (and_4_out, skip_nq, fetch_nq);
  Multiplexer multiplexer_2 (.sel(multiplexer_1_out[1]), .in_0(C), .in_1(Z), .out(multiplexer_2_out));
  and and_5 (eR1, multiplexer_1_out[0], ~multiplexer_1_out[1], and_2_out);  // And
  and and_6 (and_6_out, offset[2], and_11_out);
  and and_7 (and_7_out, ~offset[1], and_4_out, offset[3]);  // And
  xnor xnor_1 (xnor_1_out, multiplexer_1_out[0], multiplexer_2_out);
  Multiplexer #(.Bits(4)) multiplexer_3 (.sel(and_11_out), .in_0(offset), .in_1(4'b1100), .out(multiplexer_3_out));
  and and_8 (and_8_out, multiplexer_1_out_2[0], multiplexer_1_out_2[1], and_4_out);
  and and_9 (eR2, ~multiplexer_1_out[0], multiplexer_1_out[1], and_2_out);  // And
  and and_10 (wr, ~offset[2], offset[0], and_7_out);  // And
  and and_11 (and_11_out, ~offset[0], and_7_out);  // And
  Multiplexer #(.Bits(4)) multiplexer_4 (.sel(and_8_out), .in_0(multiplexer_3_out), .in_1(4'b0110), .out(op));
  and and_12 (eF, ~wr, ~and_8_out, and_4_out);  // And
  and and_13 (and_13_out, xnor_1_out, and_8_out);
  and and_14 (and_14_out, multiplexer_1_out[0], multiplexer_1_out[1], and_2_out);
  Multiplexer #(.Bits(2)) multiplexer_5 (.sel(and_8_out), .in_0(multiplexer_1_out), .in_1(2'b11), .out(sA));
  Multiplexer #(.Bits(2)) multiplexer_6 (.sel(or_3_out), .in_0(multiplexer_1_out_2), .in_1(2'b11), .out(sB));
  or or_2 (ePC, and_13_out, and_14_out, or_1_out);
  or or_3 (or_3_out, or_1_out, and_6_out);
  Register #(.Bits(8)) IR (.D(ramdualport_1_d), .C(clock), .en(eI), .Q(instr));
  Register #(.Bits(8)) r0 (.D(alu_1_r), .C(clock), .en(eR0), .Q(r0_q));
  Register #(.Bits(8)) r1 (.D(alu_1_r), .C(clock), .en(eR1), .Q(r1_q));
  Register #(.Bits(8)) r2 (.D(alu_1_r), .C(clock), .en(eR2), .Q(r2_q));
  Register #(.Bits(8)) PC (.D(alu_1_r), .C(clock), .en(ePC), .Q(PC_q));
  Multiplexer #(.Selector_Bits(2), .Bits(8)) multiplexer_7 (
    .sel(sA), .in_0(r0_q), .in_1(r1_q), .in_2(r2_q), .in_3({4'b0000, offset}), .out(multiplexer_7_out));
  Multiplexer #(.Selector_Bits(2), .Bits(8)) multiplexer_8 (
    .sel(sB), .in_0(r0_q), .in_1(r1_q), .in_2(r2_q), .in_3(PC_q), .out(multiplexer_8_out));
  and and_15 (and_15_out, multiplexer_8_out[0], multiplexer_8_out[1], multiplexer_8_out[2], multiplexer_8_out[3], multiplexer_8_out[4], multiplexer_8_out[5], multiplexer_8_out[6], multiplexer_8_out[7]);
  RAMDualPort #(.AddrBits(8), .isProgramMemory("true"), .Bits(8)) ramdualport_1 (
    .A(multiplexer_8_out), .Din(multiplexer_7_out), .str(wr), .C(clock), .ld(1'b1), .D(ramdualport_1_d));
  alu alu_1 (
    .op(op), .A(multiplexer_7_out), .B(multiplexer_8_out), .R(alu_1_r), .clk(clock), .Z(Z), .C(C),
    .eFlags(eF), .M(ramdualport_1_d));
  and and_16 (and_16_out, and_15_out, wr);
  Terminal terminal_1 (.D(multiplexer_7_out), .C(clock), .en(and_16_out));

  // Notes on the sheet:
  //   clock: Hz: 100
endmodule
