// Digital circuit ncpu16.dig as structural Verilog
// A very simple 16 bit processor
module ncpu16 (
  input  reset,
  input  clock,
  input  [15:0] dIn,
  output [15:0] address,
  output wr,
  output rd,
  output [15:0] dOut
);

  wire C, IR3, IR4, IR5, mem, or_1_out, or_3_out, or_4_out, or_5_out, w0, w1, w2, w3, w4, w5, w6, wPC, Z;
  wire [2:0] rA, rB;
  wire [13:0] multiplexer_3_out_2;
  wire [15:0] add_1_s, and_1_out, multiplexer_1_out, multiplexer_3_out, multiplexer_4_out, multiplexer_5_out,
       not_1_out, offset, or_2_out, PC_q, r0_q, r1_q, r2_q, r3_q, r4_q, r5_q, r6_q, xor_1_out;

  Multiplexer #(.Bits(16)) multiplexer_1 (.sel(mem), .in_0(address), .in_1(dIn), .out(multiplexer_1_out));
  Register #(.Bits(16)) r0 (.D(multiplexer_1_out), .C(clock), .en(w0), .Q(r0_q));
  Register #(.Bits(16)) r1 (.D(multiplexer_1_out), .C(clock), .en(w1), .Q(r1_q));
  Register #(.Bits(16)) r2 (.D(multiplexer_1_out), .C(clock), .en(w2), .Q(r2_q));
  Register #(.Bits(16)) r3 (.D(multiplexer_1_out), .C(clock), .en(w3), .Q(r3_q));
  Register #(.Bits(16)) r4 (.D(multiplexer_1_out), .C(clock), .en(w4), .Q(r4_q));
  Register #(.Bits(16)) r5 (.D(multiplexer_1_out), .C(clock), .en(w5), .Q(r5_q));
  Register #(.Bits(16)) r6 (.D(multiplexer_1_out), .C(clock), .en(w6), .Q(r6_q));
  Register #(.Bits(16)) PC (.D(multiplexer_1_out), .C(clock), .en(wPC), .Q(PC_q));
  Multiplexer #(.Selector_Bits(3), .Bits(16)) multiplexer_2 (
    .sel(rA), .in_0(r0_q), .in_1(r1_q), .in_2(r2_q), .in_3(r3_q), .in_4(r4_q), .in_5(r5_q), .in_6(r6_q),
    .in_7(PC_q), .out(dOut));
  Multiplexer #(.Selector_Bits(3), .Bits(16)) multiplexer_3 (
    .sel(rB), .in_0(r0_q), .in_1(r1_q), .in_2(r2_q), .in_3(r3_q), .in_4(r4_q), .in_5(r5_q), .in_6(r6_q),
    .in_7(PC_q), .out({multiplexer_3_out[15], multiplexer_3_out_2, multiplexer_3_out[0]}));
  or or_1 (or_1_out, address[0], address[1], address[2], address[3]);
  assign and_1_out = dOut & {multiplexer_3_out[15], multiplexer_3_out_2, multiplexer_3_out[0]};  // And and_1, 16 bits wide
  assign or_2_out = dOut | {multiplexer_3_out[15], multiplexer_3_out_2, multiplexer_3_out[0]};  // Or or_2, 16 bits wide
  assign xor_1_out = dOut ^ {multiplexer_3_out[15], multiplexer_3_out_2, multiplexer_3_out[0]};  // XOr xor_1, 16 bits wide
  assign not_1_out = ~{multiplexer_3_out[15], multiplexer_3_out_2, multiplexer_3_out[0]};  // Not not_1, 16 bits wide
  or or_3 (or_3_out, address[4], address[5], address[6], address[7]);
  Multiplexer #(.Bits(16)) multiplexer_4 (.sel(mem), .in_0(dOut), .in_1(offset), .out(multiplexer_4_out));
  Multiplexer #(.Bits(16)) multiplexer_5 (
    .sel(IR3), .in_0({multiplexer_3_out[15], multiplexer_3_out_2, multiplexer_3_out[0]}), .in_1(not_1_out),
    .out(multiplexer_5_out));
  Add #(.Bits(16)) add_1 (.a(multiplexer_4_out), .b(multiplexer_5_out), .c_i(IR3), .s(add_1_s), .c_o(C));
  or or_4 (or_4_out, address[8], address[9], address[10], address[11]);
  nor nor_1 (Z, or_1_out, or_3_out, or_4_out, or_5_out);
  or or_5 (or_5_out, address[12], address[13], address[14], address[15]);
  Multiplexer #(.Selector_Bits(3), .Bits(16)) multiplexer_6 (
    .sel({IR3, IR4, IR5}), .in_0(add_1_s), .in_1(add_1_s),
    .in_2({{2{multiplexer_3_out[15]}}, multiplexer_3_out_2}),
    .in_3({multiplexer_3_out_2[6:0], multiplexer_3_out[0], multiplexer_3_out[15], multiplexer_3_out_2[13:7]}),
    .in_4({multiplexer_3_out[15], multiplexer_3_out_2, multiplexer_3_out[0]}), .in_5(and_1_out),
    .in_6(or_2_out), .in_7(xor_1_out), .out(address));

  // Other names for the same wires on the sheet: N = address[15]

  // Notes on the sheet:
  //   address: selects memory word to read or write
  //   wr: this cycle will write a word to memory
  //   rd: this cycle will read a word from memory
  //   dOut: data to memory
  //   dIn: data from memory
endmodule
