// Digital circuit system.dig as structural Verilog
module system (
  input  clock
);

  wire ncpu16_1_wr, not_1_out, reset_out;
  wire [15:0] blockramdualport_1_d, ncpu16_1_address, ncpu16_1_dout, termcnt_1_dout;

  ncpu16 ncpu16_1 (
    .reset(reset_out), .clock(clock), .dIn(termcnt_1_dout), .address(ncpu16_1_address), .wr(ncpu16_1_wr),
    .dOut(ncpu16_1_dout));  // open: rd
  DipSwitch reset (.out(reset_out));
  BlockRAMDualPort #(.AddrBits(16), .isProgramMemory("true"), .Bits(16)) blockramdualport_1 (
    .A(ncpu16_1_address), .Din(ncpu16_1_dout), .str(ncpu16_1_wr), .C(clock), .D(blockramdualport_1_d));
  termcnt termcnt_1 (
    .relogio(clock), .write(ncpu16_1_wr), .read(not_1_out), .Addr({{16{1'b1}}, ncpu16_1_address}),
    .dMemOut(blockramdualport_1_d), .dIn(ncpu16_1_dout), .dOut(termcnt_1_dout));  // open: cnt
  not not_1 (not_1_out, ncpu16_1_wr);
endmodule
