// Digital circuit darkriscvTerm.dig as structural Verilog
module darkriscvTerm (
  input  clock,
  output idle,
  output [3:0] debug,
  output [31:0] cnt
);

  wire and_1_out, and_2_out, and_3_out, and_4_out, reset_out, u_darkriscv_rd, u_darkriscv_wr;
  wire [1:0] u_darkriscv_daddr;
  wire [3:0] u_darkriscv_be;
  wire [7:0] m0_d, m1_d, m2_d, m3_d;
  wire [13:0] u_darkriscv_iaddr_2;
  wire [15:0] termcnt_1_dout, u_darkriscv_datao, u_darkriscv_datao_2;
  wire [29:0] u_darkriscv_daddr_2;
  wire [31:0] instructions_d, u_darkriscv_iaddr;

  DipSwitch reset (.out(reset_out));
  darkriscv #(.applicationType("IVERILOG"), .CodeFile("/home/jecel/mygit/digitalCPUzoo/RV-Wrappers/src/darkriscv/darkriscv.v")) u_darkriscv (
    .RES(reset_out), .CLK(clock), .HLT(1'b0), .IDATA(instructions_d), .DATAI({m3_d, m2_d, termcnt_1_dout}),
    .IADDR({u_darkriscv_iaddr[31:16], u_darkriscv_iaddr_2, u_darkriscv_iaddr[1:0]}),
    .DATAO({u_darkriscv_datao_2, u_darkriscv_datao}), .DADDR({u_darkriscv_daddr_2, u_darkriscv_daddr}),
    .BE(u_darkriscv_be), .WR(u_darkriscv_wr), .RD(u_darkriscv_rd), .IDLE(idle), .DEBUG(debug));
  ROM #(.AddrBits(14), .isProgramMemory("true"), .Bits(32)) instructions (
    .A(u_darkriscv_iaddr_2), .sel(1'b1), .D(instructions_d));
  termcnt termcnt_1 (
    .relogio(clock), .write(u_darkriscv_wr), .read(u_darkriscv_rd), .Addr({2'b11, u_darkriscv_daddr_2}),
    .dMemOut({m1_d, m0_d}), .dIn(u_darkriscv_datao), .dOut(termcnt_1_dout), .cnt(cnt));
  and and_1 (and_1_out, u_darkriscv_wr, u_darkriscv_be[0]);
  and and_2 (and_2_out, u_darkriscv_wr, u_darkriscv_be[1]);
  and and_3 (and_3_out, u_darkriscv_wr, u_darkriscv_be[2]);
  and and_4 (and_4_out, u_darkriscv_wr, u_darkriscv_be[3]);
  RAMDualPort #(.AddrBits(16), .Bits(8)) m0 (
    .A(u_darkriscv_daddr_2[15:0]), .Din(u_darkriscv_datao[7:0]), .str(and_1_out), .C(clock),
    .ld(u_darkriscv_rd), .D(m0_d));
  RAMDualPort #(.AddrBits(16), .Bits(8)) m1 (
    .A(u_darkriscv_daddr_2[15:0]), .Din(u_darkriscv_datao[15:8]), .str(and_2_out), .C(clock),
    .ld(u_darkriscv_rd), .D(m1_d));
  RAMDualPort #(.AddrBits(16), .Bits(8)) m2 (
    .A(u_darkriscv_daddr_2[15:0]), .Din(u_darkriscv_datao_2[7:0]), .str(and_3_out), .C(clock),
    .ld(u_darkriscv_rd), .D(m2_d));
  RAMDualPort #(.AddrBits(16), .Bits(8)) m3 (
    .A(u_darkriscv_daddr_2[15:0]), .Din(u_darkriscv_datao_2[15:8]), .str(and_4_out), .C(clock),
    .ld(u_darkriscv_rd), .D(m3_d));

  // Notes on the sheet:
  //   clock: Hz: 2147483647
  //   instructions loads mandelbrot.hex
endmodule
