// Digital circuit glacialTerm.dig as structural Verilog
module glacialTerm (
  input  clock,
  output [31:0] cnt
);

  wire reset_out, u_glacial_mem_rd_en, u_glacial_mem_wr_en;
  wire [7:0] ramdualport_1_d, u_glacial_mem_wr_data;
  wire [15:0] termcnt_1_dout, u_glacial_mem_addr;

  DipSwitch reset (.out(reset_out));
  glacial #(.applicationType("IVERILOG"), .CodeFile("/home/jecel/mygit/digitalCPUzoo/RV-Wrappers/src/glacial/glacial.v")) u_glacial (
    .clk(clock), .reset(reset_out), .mem_rd_data(termcnt_1_dout[7:0]), .xint(1'b0), .xtick(1'b0),
    .mem_addr(u_glacial_mem_addr), .mem_rd_en(u_glacial_mem_rd_en), .mem_wr_en(u_glacial_mem_wr_en),
    .mem_wr_data(u_glacial_mem_wr_data));  // open: uart_tx
  RAMDualPort #(.AddrBits(16), .isProgramMemory("true"), .Bits(8)) ramdualport_1 (
    .A(u_glacial_mem_addr), .Din(u_glacial_mem_wr_data), .str(u_glacial_mem_wr_en), .C(clock),
    .ld(u_glacial_mem_rd_en), .D(ramdualport_1_d));
  termcnt termcnt_1 (
    .relogio(clock), .write(u_glacial_mem_wr_en), .read(u_glacial_mem_rd_en),
    .Addr({{16{1'b1}}, u_glacial_mem_addr}), .dMemOut({{8{1'b0}}, ramdualport_1_d}),
    .dIn({{8{1'b0}}, u_glacial_mem_wr_data}), .dOut(termcnt_1_dout), .cnt(cnt));

  // Notes on the sheet:
  //   clock: Hz: 200
endmodule
