// Digital circuit system.dig as structural Verilog
module system (
  input  clk,
  output [31:0] count
);

  wire dipswitch_1_out, t2h_1_rd, t2h_1_wr;
  wire [7:0] multiplexer_1_out;
  wire [15:0] ramdualaccess_1_d1, ramdualaccess_1_d2, t2h_1_addr, t2h_1_dout, t2h_1_i, termcnt_1_dout;

  DipSwitch dipswitch_1 (.out(dipswitch_1_out));
  // Probe inst on multiplexer_1_out
  t2h t2h_1 (
    .reset(dipswitch_1_out), .clock(clk), .Inst(multiplexer_1_out), .dIn(termcnt_1_dout), .I(t2h_1_i),
    .Addr(t2h_1_addr), .wr(t2h_1_wr), .rd(t2h_1_rd), .dOut(t2h_1_dout));
  // Probe I on t2h_1_i
  Multiplexer #(.Bits(8)) multiplexer_1 (
    .sel(t2h_1_i[0]), .in_0(ramdualaccess_1_d2[7:0]), .in_1(ramdualaccess_1_d2[15:8]), .out(multiplexer_1_out));
  // Probe addr on t2h_1_addr
  // Probe wr on t2h_1_wr
  // Probe rd on t2h_1_rd
  RAMDualAccess #(.AddrBits(14), .isProgramMemory("true"), .Bits(16)) ramdualaccess_1 (
    .str(t2h_1_wr), .C(clk), .ld(t2h_1_rd), .A1(t2h_1_addr[14:1]), .Din1(t2h_1_dout), .A2(t2h_1_i[14:1]),
    .D1(ramdualaccess_1_d1), .D2(ramdualaccess_1_d2));
  termcnt termcnt_1 (
    .relogio(clk), .write(t2h_1_wr), .read(t2h_1_rd), .Addr({{17{1'b1}}, t2h_1_addr[15:1]}),
    .dMemOut(ramdualaccess_1_d1), .dIn(t2h_1_dout), .dOut(termcnt_1_dout), .cnt(count));

  // Notes on the sheet:
  //   count: how many clock cycles per benchmark loop
endmodule
