// Digital circuit t2h.dig as structural Verilog
// The T2H processor is a one clock Harvard 16 bit implementation of a small subset of the Inmos Transputer
module t2h (
  input  reset,
  input  clock,
  input  [7:0] Inst,
  input  [15:0] dIn,
  output [15:0] I,
  output [15:0] Addr,
  output wr,
  output rd,
  output [15:0] dOut
);

  wire and_1_out, and_2_out, and_3_out, and_4_out, and_5_out, and_6_out, and_7_out, and_8_out, and_9_out,
       and_10_out, and_11_out, and_12_out, and_13_out, and_14_out, and_15_out, and_16_out, and_17_out,
       and_18_out, and_19_out, and_20_out, and_21_out, and_22_out, and_23_out, and_24_out, and_25_out,
       and_26_out, and_27_out, and_28_out, and_29_out, and_30_out, and_31_out, and_32_out, and_33_out,
       and_34_out, and_35_out, and_36_out, and_37_out, and_38_out, and_39_out, and_40_out, and_41_out,
       and_43_out, and_44_out, and_45_out, and_46_out, and_47_out, and_48_out, and_49_out, and_50_out,
       and_51_out, and_52_out, and_53_out, and_54_out, and_55_out, and_56_out, and_60_out, clrO, eA, eB, eC,
       eW, negO, not_1_out, not_2_out, not_4_out, or_16_out, or_17_out, or_18_out, or_19_out, or_20_out,
       or_23_out, or_24_out, or_25_out, or_26_out, s_plus, sA, sAddr, sB, xor_3_out;
  wire [0:0] multiplexer_5_out, nor_1_out;
  wire [1:0] sDout, sI;
  wire [3:0] or_21_out, sALU, xor_2_out, xor_2_out_2, xor_2_out_3, xor_2_out_4;
  wire [3:3] and_58_out;
  wire [4:0] op;
  wire [7:0] multiplexer_2_out, not_7_out;
  wire [11:0] multiplexer_4_out;
  wire [15:0] A, add_1_s, add_2_s, add_4_s, add_5_s, add_6_s, and_59_out, B, C, I_plus_1, multiplexer_3_out,
       multiplexer_6_out, multiplexer_7_out, multiplexer_8_out, multiplexer_9_out, multiplexer_10_out,
       multiplexer_11_out, or_22_out, sub_1_s, W_q, xor_1_out;
  wire [15:4] x;

  not not_1 (not_1_out, op[4]);
  not not_2 (not_2_out, op[3]);
  not not_3 (sDout[1], negO);
  not not_4 (not_4_out, op[1]);
  not not_5 (sDout[0], op[0]);
  and and_1 (and_1_out, sDout[0], op[1], negO, op[4]);
  and and_2 (and_2_out, sDout[0], not_4_out, op[3], not_1_out);
  and and_3 (and_3_out, op[0], sDout[1], op[4]);
  and and_4 (and_4_out, op[0], not_2_out);
  and and_5 (and_5_out, not_4_out, negO, op[3]);
  and and_6 (and_6_out, not_4_out, negO, not_1_out);
  and and_7 (and_7_out, negO, op[3], not_1_out);
  and and_8 (and_8_out, sDout[1], not_2_out, op[4]);
  and and_9 (and_9_out, op[0], not_4_out, sDout[1], not_2_out, not_1_out);
  and and_10 (and_10_out, sDout[0], not_4_out, negO, not_2_out, not_1_out);
  and and_11 (and_11_out, sDout[0], not_4_out, sDout[1], not_2_out, op[4]);
  and and_12 (and_12_out, sDout[0], not_4_out, negO, op[3], op[4]);
  and and_13 (and_13_out, op[0], op[1], negO, not_2_out);
  and and_14 (and_14_out, op[0], op[1], sDout[1], op[4]);
  and and_15 (and_15_out, op[0], negO, op[3], not_1_out);
  and and_16 (and_16_out, op[0], negO, not_2_out, op[4]);
  and and_17 (and_17_out, op[0], sDout[1], op[3], op[4]);
  and and_18 (and_18_out, op[1], negO, op[3], not_1_out);
  and and_19 (and_19_out, op[1], sDout[1], op[3], op[4]);
  or or_1 (eA, and_1_out, and_2_out, and_3_out, and_4_out, and_5_out, and_6_out, and_7_out, and_8_out);
  or or_2 (eB, and_9_out, and_10_out, and_11_out, and_12_out, and_13_out, and_14_out, and_15_out, and_16_out, and_17_out, and_18_out, and_19_out);
  and and_20 (and_20_out, op[0], not_4_out, sDout[1], not_2_out, not_1_out);
  and and_21 (and_21_out, sDout[0], not_4_out, negO, not_2_out, not_1_out);
  and and_22 (and_22_out, op[0], op[1], negO, not_2_out, not_1_out);
  and and_23 (and_23_out, sDout[0], op[1], sDout[1], op[3], op[4]);
  and and_24 (and_24_out, op[0], op[1], sDout[1], op[3], not_1_out);
  and and_25 (and_25_out, sDout[0], op[1], negO, op[3], op[4]);
  and and_26 (and_26_out, op[0], op[1], not_2_out, not_1_out);
  and and_27 (and_27_out, op[0], not_2_out, not_1_out);
  and and_28 (and_28_out, sDout[0], op[3]);
  and and_29 (and_29_out, op[3], op[4]);
  and and_30 (and_30_out, sDout[0], op[1], negO);
  and and_31 (and_31_out, negO, op[4]);
  and and_32 (and_32_out, not_2_out, not_1_out);
  and and_33 (and_33_out, sDout[0], negO, op[3], not_1_out);
  and and_34 (and_34_out, op[0], not_2_out, not_1_out);
  and and_35 (and_35_out, op[1], op[4]);
  and and_36 (and_36_out, op[0], not_2_out);
  and and_37 (and_37_out, op[0], op[4]);
  and and_38 (and_38_out, op[1], op[3], op[4]);
  and and_39 (and_39_out, op[0], op[4]);
  and and_40 (and_40_out, not_4_out, op[3]);
  and and_41 (and_41_out, op[3], not_1_out);
  or or_3 (eW, and_24_out, and_25_out);
  or or_4 (sALU[3], and_27_out, and_28_out, and_29_out);
  or or_5 (sALU[2], and_30_out, and_31_out, and_32_out);
  or or_6 (sALU[1], and_33_out, and_34_out, and_35_out);
  or or_7 (sALU[0], and_36_out, and_37_out, and_38_out);
  or or_8 (sB, and_39_out, and_40_out, and_41_out);
  or or_9 (eC, and_20_out, and_21_out, and_22_out, and_23_out);
  not not_6 (sA, and_26_out);
  and and_42 (clrO, sDout[0], op[1], not_2_out, not_1_out);
  and and_43 (and_43_out, op[1], sDout[1]);
  and and_44 (and_44_out, not_4_out, negO, not_2_out);
  and and_45 (and_45_out, op[1], op[3]);
  and and_46 (and_46_out, negO, not_1_out);
  and and_47 (and_47_out, op[0], op[1], negO, op[3], op[4]);
  and and_48 (and_48_out, op[0], op[1], not_2_out, not_1_out);
  and and_49 (and_49_out, sDout[0], op[1], negO, op[3], not_1_out);
  and and_50 (and_50_out, op[0], not_4_out, op[3], not_1_out);
  and and_51 (and_51_out, sDout[0], op[1], negO, not_2_out, op[4]);
  and and_52 (and_52_out, op[0], op[1], negO, op[3], op[4]);
  and and_53 (and_53_out, sDout[0], not_4_out, sDout[1], not_2_out, not_1_out);
  and and_54 (and_54_out, op[0], not_4_out, sDout[1], op[3], not_1_out);
  and and_55 (and_55_out, sDout[0], op[1], sDout[1], op[3], not_1_out);
  and and_56 (and_56_out, op[0], op[1], negO, op[3], op[4]);
  or or_10 (s_plus, and_43_out, and_44_out, and_45_out);
  or or_11 (sAddr, and_46_out, not_2_out);
  or or_12 (rd, and_47_out, and_48_out);
  or or_13 (wr, and_49_out, and_50_out);
  or or_14 (sI[1], and_51_out, and_52_out);
  or or_15 (sI[0], and_53_out, and_54_out, and_55_out, and_56_out);
  or or_16 (or_16_out, A[0], A[1], A[2], A[3]);
  or or_17 (or_17_out, A[4], A[5], A[6], A[7]);
  or or_18 (or_18_out, A[8], A[9], A[10], A[11]);
  or or_19 (or_19_out, A[12], A[13], A[14], A[15]);
  or or_20 (or_20_out, or_16_out, or_17_out, or_18_out, or_19_out);
  and and_57 (op[4], Inst[4], Inst[5], Inst[6], Inst[7]);
  and and_58 (and_58_out[3], ~Inst[4], Inst[5], or_20_out, ~Inst[6], Inst[7]);  // And
  assign or_21_out = Inst[7:4] | {4{and_58_out[3]}};  // Or or_21, 4 bits wide
  assign xor_1_out = A ^ B;  // XOr xor_1, 16 bits wide
  Add #(.Bits(16)) add_1 (.a(A), .b(B), .c_i(1'b0), .s(add_1_s));  // open: c_o
  assign and_59_out = A & B;  // And and_59, 16 bits wide
  Add #(.Bits(16)) add_2 (.a(A), .b({x, Inst[3:0]}), .c_i(1'b0), .s(add_2_s));  // open: c_o
  Sub #(.Bits(16)) sub_1 (.a(B), .b(A), .c_i(1'b0), .s(sub_1_s));  // open: c_o
  assign or_22_out = A | B;  // Or or_22, 16 bits wide
  assign {xor_2_out_4, xor_2_out_3, xor_2_out_2, xor_2_out} = A ^ {x, Inst[3:0]};  // XOr xor_2, 16 bits wide
  Multiplexer #(.Bits(4)) multiplexer_1 (.sel(op[4]), .in_0(or_21_out), .in_1(Inst[3:0]), .out({op[3], negO, op[1:0]}));
  xor xor_3 (xor_3_out, A[15], B[15]);
  Multiplexer #(.Bits(8)) multiplexer_2 (.sel(negO), .in_0(x[11:4]), .in_1(not_7_out), .out(multiplexer_2_out));
  assign not_7_out = ~x[11:4];  // Not not_7, 8 bits wide
  Multiplexer #(.Selector_Bits(4), .Bits(16)) multiplexer_3 (
    .sel(sALU), .in_0(B), .in_1({A[14:0], 1'b0}), .in_2({{2{A[15]}}, A[14:1]}), .in_3(xor_1_out),
    .in_4({x, Inst[3:0]}), .in_5(add_1_s), .in_6(I_plus_1), .in_7(and_59_out), .in_8(add_2_s),
    .in_9({{15{1'b0}}, multiplexer_5_out[0]}), .in_10({{15{1'b0}}, nor_1_out[0]}), .in_11(or_22_out),
    .in_12(sub_1_s), .in_13({A[7:0], A[15:8]}), .in_14(C), .in_15(Addr), .out(multiplexer_3_out));
  and and_60 (and_60_out, ~sub_1_s[15], ~nor_1_out[0]);  // And
  or or_23 (or_23_out, xor_2_out[0], xor_2_out[1], xor_2_out[2], xor_2_out[3]);
  or or_24 (or_24_out, xor_2_out_2[0], xor_2_out_2[1], xor_2_out_2[2], xor_2_out_2[3]);
  or or_25 (or_25_out, xor_2_out_3[0], xor_2_out_3[1], xor_2_out_3[2], xor_2_out_3[3]);
  or or_26 (or_26_out, xor_2_out_4[0], xor_2_out_4[1], xor_2_out_4[2], xor_2_out_4[3]);
  Multiplexer #(.Bits(12)) multiplexer_4 (
    .sel(clrO), .in_0({12{1'b0}}), .in_1({multiplexer_2_out, Inst[3:0]}), .out(multiplexer_4_out));
  Multiplexer multiplexer_5 (.sel(xor_3_out), .in_0(and_60_out), .in_1(A[15]), .out(multiplexer_5_out[0]));
  Register #(.Bits(12)) O (.D(multiplexer_4_out), .C(clock), .en(1'b1), .Q(x));
  nor nor_1 (nor_1_out[0], or_23_out, or_24_out, or_25_out, or_26_out);
  Add #(.Bits(16)) add_3 (.a(I), .b({16{1'b0}}), .c_i(1'b1), .s(I_plus_1));  // open: c_o
  Add #(.Bits(16)) add_4 (.a(I), .b({x, Inst[3:0]}), .c_i(1'b1), .s(add_4_s));  // open: c_o
  Add #(.Bits(16)) add_5 (.a({x, Inst[3:0]}), .b(W_q), .c_i(1'b0), .s(add_5_s));  // open: c_o
  // Probe x on {x, Inst[3:0]}
  Multiplexer #(.Selector_Bits(2), .Bits(16)) multiplexer_6 (
    .sel(sI), .in_0(I_plus_1), .in_1(add_4_s), .in_2(A), .in_3(dIn), .out(multiplexer_6_out));
  Multiplexer #(.Bits(16)) multiplexer_7 (.sel(sA), .in_0(dIn), .in_1(multiplexer_3_out), .out(multiplexer_7_out));
  Multiplexer #(.Bits(16)) multiplexer_8 (.sel(sB), .in_0(A), .in_1(C), .out(multiplexer_8_out));
  Multiplexer #(.Bits(16)) multiplexer_9 (.sel(sDout[0]), .in_0(add_5_s), .in_1(A), .out(multiplexer_9_out));
  Multiplexer #(.Bits(16)) multiplexer_10 (.sel(s_plus), .in_0(W_q), .in_1(A), .out(multiplexer_10_out));
  Multiplexer #(.Bits(16)) multiplexer_11 (
    .sel(reset), .in_0(multiplexer_6_out), .in_1({16{1'b0}}), .out(multiplexer_11_out));
  Register #(.Bits(16)) u_I (.D(multiplexer_11_out), .C(clock), .en(1'b1), .Q(I));
  Register #(.Bits(16)) W (.D(multiplexer_9_out), .C(clock), .en(eW), .Q(W_q));
  Add #(.Bits(16)) add_6 (
    .a(multiplexer_10_out), .b({x[14:4], Inst[3:0], 1'b0}), .c_i(1'b0), .s(add_6_s));  // open: c_o
  Register #(.Bits(16)) u_A (.D(multiplexer_7_out), .C(clock), .en(eA), .Q(A));
  Register #(.Bits(16)) u_B (.D(multiplexer_8_out), .C(clock), .en(eB), .Q(B));
  Register #(.Bits(16)) u_C (.D(B), .C(clock), .en(eC), .Q(C));
  // Probe W on W_q
  // Probe B on B
  // Probe C on C
  Multiplexer #(.Bits(16)) multiplexer_12 (.sel(sAddr), .in_0(W_q), .in_1(add_6_s), .out(Addr));
  Multiplexer #(.Selector_Bits(2), .Bits(16)) multiplexer_13 (
    .sel(sDout), .in_0(A), .in_1(B), .in_2(I_plus_1), .in_3(I_plus_1), .out(dOut));
  // Probe A on A

  // Other names for the same wires on the sheet: op[2] = negO; x[3:0] = Inst[3:0]; sW = sDout[0]

  // Notes on the sheet:
  //   I: program counter
  //   Addr: Data memory address
  //   wr: write to memory
  //   rd: indicates a read cycle from memory
  //   Inst: instruction to be executed
  //   dIn: data from memory
  //   dOut: data output to memory
endmodule
