// Digital circuit t2hcontrol.dig as structural Verilog
module t2hcontrol (
  input  op4,
  input  op3,
  input  op2,
  input  op1,
  input  op0,
  output eA,
  output eB,
  output eC,
  output eW,
  output sA,
  output sALU3,
  output sALU2,
  output sALU1,
  output sALU0,
  output sB,
  output clrO,
  output negO,
  output sW,
  output s_plus,
  output sAddr,
  output rd,
  output wr,
  output sDout1,
  output sDout0,
  output sI1,
  output sI0
);

  wire and_1_out, and_2_out, and_3_out, and_4_out, and_5_out, and_6_out, and_7_out, and_8_out, and_9_out,
       and_10_out, and_11_out, and_12_out, and_13_out, and_14_out, and_15_out, and_16_out, and_17_out,
       and_18_out, and_19_out, and_20_out, and_21_out, and_22_out, and_23_out, and_24_out, and_25_out,
       and_26_out, and_27_out, and_28_out, and_29_out, and_30_out, and_31_out, and_32_out, and_33_out,
       and_34_out, and_35_out, and_36_out, and_37_out, and_38_out, and_39_out, and_40_out, and_41_out,
       and_43_out, and_44_out, and_45_out, and_46_out, and_47_out, and_48_out, and_49_out, and_50_out,
       and_51_out, and_52_out, and_53_out, and_54_out, and_55_out, and_56_out, not_1_out, not_2_out,
       not_4_out;

  not not_1 (not_1_out, op4);
  not not_2 (not_2_out, op3);
  not not_3 (sDout1, op2);
  not not_4 (not_4_out, op1);
  not not_5 (sDout0, op0);
  and and_1 (and_1_out, sDout0, op1, op2, op4);
  and and_2 (and_2_out, sDout0, not_4_out, op3, not_1_out);
  and and_3 (and_3_out, op0, sDout1, op4);
  and and_4 (and_4_out, op0, not_2_out);
  and and_5 (and_5_out, not_4_out, op2, op3);
  and and_6 (and_6_out, not_4_out, op2, not_1_out);
  and and_7 (and_7_out, op2, op3, not_1_out);
  and and_8 (and_8_out, sDout1, not_2_out, op4);
  and and_9 (and_9_out, op0, not_4_out, sDout1, not_2_out, not_1_out);
  and and_10 (and_10_out, sDout0, not_4_out, op2, not_2_out, not_1_out);
  and and_11 (and_11_out, sDout0, not_4_out, sDout1, not_2_out, op4);
  and and_12 (and_12_out, sDout0, not_4_out, op2, op3, op4);
  and and_13 (and_13_out, op0, op1, op2, not_2_out);
  and and_14 (and_14_out, op0, op1, sDout1, op4);
  and and_15 (and_15_out, op0, op2, op3, not_1_out);
  and and_16 (and_16_out, op0, op2, not_2_out, op4);
  and and_17 (and_17_out, op0, sDout1, op3, op4);
  and and_18 (and_18_out, op1, op2, op3, not_1_out);
  and and_19 (and_19_out, op1, sDout1, op3, op4);
  and and_20 (and_20_out, op0, not_4_out, sDout1, not_2_out, not_1_out);
  and and_21 (and_21_out, sDout0, not_4_out, op2, not_2_out, not_1_out);
  and and_22 (and_22_out, op0, op1, op2, not_2_out, not_1_out);
  and and_23 (and_23_out, sDout0, op1, sDout1, op3, op4);
  and and_24 (and_24_out, op0, op1, sDout1, op3, not_1_out);
  and and_25 (and_25_out, sDout0, op1, op2, op3, op4);
  and and_26 (and_26_out, op0, op1, not_2_out, not_1_out);
  and and_27 (and_27_out, op0, not_2_out, not_1_out);
  and and_28 (and_28_out, sDout0, op3);
  and and_29 (and_29_out, op3, op4);
  and and_30 (and_30_out, sDout0, op1, op2);
  and and_31 (and_31_out, op2, op4);
  and and_32 (and_32_out, not_2_out, not_1_out);
  and and_33 (and_33_out, sDout0, op2, op3, not_1_out);
  and and_34 (and_34_out, op0, not_2_out, not_1_out);
  and and_35 (and_35_out, op1, op4);
  and and_36 (and_36_out, op0, not_2_out);
  and and_37 (and_37_out, op0, op4);
  and and_38 (and_38_out, op1, op3, op4);
  and and_39 (and_39_out, op0, op4);
  and and_40 (and_40_out, not_4_out, op3);
  and and_41 (and_41_out, op3, not_1_out);
  and and_42 (clrO, sDout0, op1, not_2_out, not_1_out);
  and and_43 (and_43_out, op1, sDout1);
  and and_44 (and_44_out, not_4_out, op2, not_2_out);
  and and_45 (and_45_out, op1, op3);
  and and_46 (and_46_out, op2, not_1_out);
  and and_47 (and_47_out, op0, op1, op2, op3, op4);
  and and_48 (and_48_out, op0, op1, not_2_out, not_1_out);
  and and_49 (and_49_out, sDout0, op1, op2, op3, not_1_out);
  and and_50 (and_50_out, op0, not_4_out, op3, not_1_out);
  and and_51 (and_51_out, sDout0, op1, op2, not_2_out, op4);
  and and_52 (and_52_out, op0, op1, op2, op3, op4);
  and and_53 (and_53_out, sDout0, not_4_out, sDout1, not_2_out, not_1_out);
  and and_54 (and_54_out, op0, not_4_out, sDout1, op3, not_1_out);
  and and_55 (and_55_out, sDout0, op1, sDout1, op3, not_1_out);
  and and_56 (and_56_out, op0, op1, op2, op3, op4);
  or or_1 (eW, and_24_out, and_25_out);
  or or_2 (sALU3, and_27_out, and_28_out, and_29_out);
  or or_3 (sALU2, and_30_out, and_31_out, and_32_out);
  or or_4 (sALU1, and_33_out, and_34_out, and_35_out);
  or or_5 (sALU0, and_36_out, and_37_out, and_38_out);
  or or_6 (sB, and_39_out, and_40_out, and_41_out);
  or or_7 (s_plus, and_43_out, and_44_out, and_45_out);
  or or_8 (sAddr, and_46_out, not_2_out);
  or or_9 (rd, and_47_out, and_48_out);
  or or_10 (wr, and_49_out, and_50_out);
  or or_11 (sI1, and_51_out, and_52_out);
  or or_12 (eA, and_1_out, and_2_out, and_3_out, and_4_out, and_5_out, and_6_out, and_7_out, and_8_out);
  or or_13 (eB, and_9_out, and_10_out, and_11_out, and_12_out, and_13_out, and_14_out, and_15_out, and_16_out, and_17_out, and_18_out, and_19_out);
  or or_14 (eC, and_20_out, and_21_out, and_22_out, and_23_out);
  not not_6 (sA, and_26_out);
  or or_15 (sI0, and_53_out, and_54_out, and_55_out, and_56_out);

  assign negO = op2;
  assign sW = sDout0;
endmodule
