// Digital circuit vg.dig as structural Verilog
// A trivial videogame using a T2H processor and a videotext style HDMI output
module vg (
  input  clk
);

  wire and_1_out, and_2_out, and_3_out, and_4_out, and_5_out, av_1_h, av_1_v, dipswitch_1_out, t2h_1_rd,
       t2h_1_wr;
  wire [7:0] av_1_b, av_1_g, av_1_r, multiplexer_1_out;
  wire [11:0] av_1_addr;
  wire [15:0] FB_d2, Main_d1, Main_d2, t2h_1_addr, t2h_1_dout, t2h_1_i;

  DipSwitch dipswitch_1 (.out(dipswitch_1_out));
  // Probe inst on multiplexer_1_out
  t2h t2h_1 (
    .reset(dipswitch_1_out), .clock(clk), .Inst(multiplexer_1_out), .dIn(Main_d1), .I(t2h_1_i),
    .Addr(t2h_1_addr), .wr(t2h_1_wr), .rd(t2h_1_rd), .dOut(t2h_1_dout));
  av av_1 (
    .dIn(FB_d2), .pclk(clk), .R(av_1_r), .G(av_1_g), .B(av_1_b), .H(av_1_h), .V(av_1_v), .Addr(av_1_addr));  // open: X, Y, sclk, left, right, read
  // Probe I on t2h_1_i
  Multiplexer #(.Bits(8)) multiplexer_1 (
    .sel(t2h_1_i[0]), .in_0(Main_d2[7:0]), .in_1(Main_d2[15:8]), .out(multiplexer_1_out));
  VGA vga_1 (.R(av_1_r), .G(av_1_g), .B(av_1_b), .H(av_1_h), .V(av_1_v), .C(clk));
  RAMDualAccess #(.AddrBits(15), .isProgramMemory("true"), .Bits(16)) Main (
    .str(and_2_out), .C(clk), .ld(and_3_out), .A1(t2h_1_addr[15:1]), .Din1(t2h_1_dout), .A2(t2h_1_i[15:1]),
    .D1(Main_d1), .D2(Main_d2));
  RAMDualAccess #(.AddrBits(12), .Bits(16)) FB (
    .str(and_4_out), .C(clk), .ld(and_5_out), .A1(t2h_1_addr[12:1]), .Din1(t2h_1_dout), .A2(av_1_addr),
    .D1(Main_d1), .D2(FB_d2));
  and and_1 (and_1_out, t2h_1_addr[13], t2h_1_addr[14], t2h_1_addr[15]);
  and and_2 (and_2_out, t2h_1_wr, ~and_1_out);  // And
  and and_3 (and_3_out, t2h_1_rd, ~and_1_out);  // And
  and and_4 (and_4_out, t2h_1_wr, and_1_out);
  and and_5 (and_5_out, t2h_1_rd, and_1_out);

  // Notes on the sheet:
  //   clk: Hz: 2147483647
endmodule
