// Digital circuit adapt.dig as structural Verilog
// adapts values out of registers for the ALU
module adapt (
  input  [15:0] Da,
  input  [15:0] Db,
  input  [11:0] topImm,
  input  [3:0] rD,
  input  [3:0] rS2,
  input  even,
  input  const2,
  input  selImm,
  input  selConst,
  input  Azero,
  input  immLow,
  output [15:0] A,
  output [15:0] B,
  output alt
);

  wire [0:0] and_1_out;
  wire [3:1] multiplexer_1_out;
  wire [15:0] multiplexer_3_out;

  Multiplexer #(.Bits(4)) multiplexer_1 (.sel(immLow), .in_0(rS2), .in_1(rD), .out({multiplexer_1_out, alt}));
  and and_1 (and_1_out[0], ~even, alt);  // And
  Multiplexer #(.Bits(16)) multiplexer_2 (.sel(Azero), .in_0(Da), .in_1({16{1'b0}}), .out(A));
  Multiplexer #(.Bits(16)) multiplexer_3 (
    .sel(selConst), .in_0(Db), .in_1({{14{1'b0}}, const2, 1'b0}), .out(multiplexer_3_out));
  Multiplexer #(.Bits(16)) multiplexer_4 (
    .sel(selImm), .in_0(multiplexer_3_out), .in_1({topImm, multiplexer_1_out, and_1_out[0]}), .out(B));

  // Notes on the sheet:
  //   topImm: bits saved from prefix
  //   rD: rD field from current instruction
  //   rS2: rS2 field from instruction
  //   even: force even values for PC math
  //   alt: lowest bit indicates alternative branch instruction
  //   const2: changes 0 to 2 to increment the PC
  //   selImm: operand B is an immediate
  //   selConst: selects either 0 or 2
endmodule
