// Digital circuit alu.dig as structural Verilog
// implements all the math and logic functions
module alu (
  input  [15:0] A,
  input  [15:0] B,
  input  sub,
  input  [1:0] logSelect,
  input  \logic ,
  output [15:0] R,
  output NE,
  output GE
);

  wire or_2_out, or_3_out, or_4_out, or_5_out;
  wire [15:0] add_1_s, and_1_out, multiplexer_1_out, or_1_out, xor_1_out, xor_2_out;

  assign and_1_out = A & B;  // And and_1, 16 bits wide
  assign or_1_out = A | B;  // Or or_1, 16 bits wide
  assign xor_1_out = A ^ B;  // XOr xor_1, 16 bits wide
  assign xor_2_out = {16{sub}} ^ B;  // XOr xor_2, 16 bits wide
  Add #(.Bits(16)) add_1 (.a(A), .b(xor_2_out), .c_i(sub), .s(add_1_s), .c_o(GE));
  Multiplexer #(.Bits(16), .Selector_Bits(2)) multiplexer_1 (
    .sel(logSelect), .in_0({B[15], A[15:1]}), .in_1(and_1_out), .in_2(or_1_out), .in_3(xor_1_out),
    .out(multiplexer_1_out));
  Multiplexer #(.Bits(16)) multiplexer_2 (.sel(\logic ), .in_0(add_1_s), .in_1(multiplexer_1_out), .out(R));
  or or_2 (or_2_out, R[0], R[1], R[2], R[3]);
  or or_3 (or_3_out, R[4], R[5], R[6], R[7]);
  or or_4 (or_4_out, R[8], R[9], R[10], R[11]);
  or or_5 (or_5_out, R[12], R[13], R[14], R[15]);
  or or_6 (NE, or_2_out, or_3_out, or_4_out, or_5_out);

  // Notes on the sheet:
  //   R: result
  //   A: first operand
  //   B: second operand
  //   sub: changes addition to subtraction
  //   logSelect: selects between logic functions
  //   logic: logic functions instead of addition
  //   NE: when used with a subtraction indicates that the operands are Not Equal
  //   GE: when used with a subtraction, indicates A>= B signed
endmodule
