// Digital circuit bytes.dig as structural Verilog
// converts internal word data into bytes for LB, LBU and SB instructions
module bytes (
  input  [15:0] dIn,
  input  sign,
  input  word,
  input  A0,
  input  [15:0] fromRS2,
  output [15:0] dOut,
  output [15:0] toRD
);

  wire [15:0] multiplexer_4_out;
  wire [15:7] and_1_out;
  wire [15:8] multiplexer_1_out, multiplexer_2_out, multiplexer_3_out, multiplexer_5_out, undriven,
       undriven_2, undriven_3, undriven_4;

  and and_1 (and_1_out[7], toRD[7], sign);
  Multiplexer #(.Bits(16)) multiplexer_1 (
    .sel(A0), .in_0({undriven_2, dIn[7:0]}), .in_1({undriven, dIn[15:8]}),
    .out({multiplexer_1_out, toRD[7:0]}));
  Multiplexer #(.Bits(16)) multiplexer_2 (
    .sel(word), .in_0({and_1_out, {7{and_1_out[7]}}}), .in_1({undriven, dIn[15:8]}),
    .out({multiplexer_2_out, toRD[15:8]}));
  Multiplexer #(.Bits(16)) multiplexer_3 (
    .sel(A0), .in_0({undriven_4, fromRS2[7:0]}), .in_1({undriven_2, dIn[7:0]}),
    .out({multiplexer_3_out, dOut[7:0]}));
  Multiplexer #(.Bits(16)) multiplexer_4 (
    .sel(A0), .in_0({undriven, dIn[15:8]}), .in_1({undriven_4, fromRS2[7:0]}), .out(multiplexer_4_out));
  Multiplexer #(.Bits(16)) multiplexer_5 (
    .sel(word), .in_0(multiplexer_4_out), .in_1({undriven_3, fromRS2[15:8]}),
    .out({multiplexer_5_out, dOut[15:8]}));
  // Pins of 8 and 16 bits meet at {undriven_4, fromRS2[7:0]}
  // Pins of 8 and 16 bits meet at {undriven_2, dIn[7:0]}
  // Pins of 8 and 16 bits meet at {multiplexer_3_out, dOut[7:0]}
  // Pins of 8 and 16 bits meet at {undriven_3, fromRS2[15:8]}
  // Pins of 8 and 16 bits meet at {multiplexer_5_out, dOut[15:8]}
  // Pins of 8 and 16 bits meet at {undriven, dIn[15:8]}
  // Pins of 8 and 16 bits meet at {multiplexer_1_out, toRD[7:0]}
  // Pins of 8 and 16 bits meet at {and_1_out, {7{and_1_out[7]}}}
  // Pins of 8 and 16 bits meet at {multiplexer_2_out, toRD[15:8]}

  // Notes on the sheet:
  //   dOut: word to be sent to memory
  //   dIn: word coming from memory
  //   toRD: bytes to word
  //   sign: indicates that the byte extension should be signed
  //   word: word memory access (not byte)
  //   A0: selects between even and odd bytes
  //   fromRS2: word data from register (top 8 bits will be ignored on byte access)
endmodule
