// Digital circuit controlUnit.dig as structural Verilog
// generates control signals for datapath
module controlUnit (
  input  clock,
  input  reset,
  input  [15:0] dIn,
  input  NE,
  input  GE,
  output wr,
  output rd,
  output sign,
  output word,
  output sub,
  output \logic ,
  output [1:0] logSelect,
  output [15:0] Imm,
  output selImm,
  output Azero,
  output we,
  output [3:0] Rw,
  output [3:0] Ra,
  output [3:0] Rb,
  output selRd,
  output slt
);

  wire and_1_out, and_2_out, and_3_out, and_4_out, and_7_out, and_9_out, and_10_out, and_11_out, and_12_out,
       and_13_out, and_14_out, and_19_out, and_21_out, and_22_out, branch, cond, d_ff_1_q, d_ff_2_q, E, EJ,
       EJorB, F, FJorBT, FnotBT, imm_t, IR2, IR3, multiplexer_2_out, or_1_out, or_5_out, or_9_out, or_10_out,
       or_11_out, prefix_q, xor_1_out, zD, zS1, zS2;
  wire [0:0] and_24_out;
  wire [1:1] or_7_out;
  wire [3:0] multiplexer_3_out;
  wire [4:0] fetchpla_1_selimm;
  wire [11:0] IM_q, multiplexer_1_out;
  wire [12:0] execpla_1_selimm, multiplexer_5_out;
  wire [15:8] IR_q;

  and and_1 (and_1_out, E, zS1);
  and and_2 (and_2_out, ~EJorB, E, imm_t);  // And
  Multiplexer #(.Bits(12)) multiplexer_1 (
    .sel(d_ff_2_q), .in_0({IR_q, Rb}), .in_1({12{1'b0}}), .out(multiplexer_1_out));
  and and_3 (and_3_out, ~dIn[0], ~dIn[1], ~dIn[2], ~dIn[3], F);  // And
  and and_4 (and_4_out, ~IR3, ~IR2, ~logSelect[1], ~logSelect[0]);  // And
  and and_5 (EJorB, ~IR3, ~IR2, E);  // And
  Multiplexer multiplexer_2 (.sel(logSelect[0]), .in_0(NE), .in_1(GE), .out(multiplexer_2_out));
  xor xor_1 (xor_1_out, multiplexer_2_out, ~multiplexer_3_out[0]);  // XOr
  D_FF d_ff_1 (.D(reset), .C(clock), .Q(d_ff_1_q));  // open: nQ
  Register #(.Bits(16)) IR (.D(dIn), .C(clock), .en(F), .Q({IR_q, Rb, IR3, IR2, logSelect}));
  Register #(.Bits(12)) IM (.D(multiplexer_1_out), .C(clock), .en(F), .Q(IM_q));
  D_FF fetch (.D(or_1_out), .C(clock), .Q(F), .nQ(E));
  // Probe IR on {IR_q, Rb, IR3, IR2, logSelect}
  or or_1 (or_1_out, E, d_ff_1_q, and_3_out);
  Register prefix (.D(and_4_out), .C(clock), .en(F), .Q(prefix_q));
  // Probe IM on IM_q
  D_FF d_ff_2 (.D(E), .C(clock), .Q(d_ff_2_q));  // open: nQ
  and and_6 (zS2, E, ~Rb[0], ~Rb[1], ~Rb[2], ~Rb[3], ~and_2_out);  // And
  or or_2 (imm_t, prefix_q, ~IR3);  // Or
  and and_7 (and_7_out, ~IR3, ~IR2, ~logSelect[1], logSelect[0]);  // And
  and and_8 (branch, ~IR3, ~IR2, logSelect[1]);  // And
  // Probe fetch on F
  D_FF d_ff_3 (.D(xor_1_out), .C(clock), .Q(cond));  // open: nQ
  and and_9 (and_9_out, E, ~IR2, ~logSelect[1], ~logSelect[0]);  // And
  and and_10 (and_10_out, E, ~IR3, IR2);  // And
  and and_11 (and_11_out, and_7_out, multiplexer_3_out[0]);
  or or_3 (selRd, and_9_out, and_10_out);
  and and_12 (and_12_out, F, ~and_11_out);  // And
  and and_13 (and_13_out, F, ~d_ff_1_q);  // And
  and and_14 (and_14_out, F, ~FJorBT);  // And
  or or_4 (Azero, d_ff_1_q, and_1_out);
  or or_5 (or_5_out, branch, zD);
  r0 r0_1 (.rin(IR_q[11:8]), .pc(or_11_out), .rout(Ra), .z(zS1));
  and and_15 (wr, E, ~IR3, IR2, logSelect[1]);  // And
  or or_6 (rd, F, selRd);
  and and_16 (sub, E, ~IR2, logSelect[1]);  // And
  and and_17 (\logic , E, IR3, IR2);
  nand nand_1 (we, E, or_5_out);
  r0 r0_2 (.rin(IR_q[15:12]), .pc(FnotBT), .rout(Rw), .z(zD));
  and and_18 (slt, E, ~IR2, logSelect[1], logSelect[0]);  // And
  and and_19 (and_19_out, F, ~IR3, logSelect[1]);  // And
  and and_20 (EJ, E, and_7_out);
  and and_21 (and_21_out, F, and_7_out);
  and and_22 (and_22_out, F, branch, cond);
  or or_7 (or_7_out[1], and_13_out, EJ);
  or or_8 (selImm, F, and_2_out);
  or or_9 (or_9_out, EJ, and_14_out, zS2);
  or or_10 (or_10_out, and_19_out, wr);
  or or_11 (or_11_out, and_12_out, EJ);
  or or_12 (FJorBT, and_21_out, and_22_out);
  // Probe BT on and_22_out
  and and_23 (FnotBT, ~and_22_out, F);  // And
  not not_1 (sign, IR3);
  Multiplexer #(.Bits(4)) multiplexer_3 (.sel(or_10_out), .in_0(Rb), .in_1(IR_q[15:12]), .out(multiplexer_3_out));
  and and_24 (and_24_out[0], ~or_7_out[1], multiplexer_3_out[0]);  // And
  Multiplexer #(.Bits(16)) multiplexer_4 (
    .sel(or_9_out), .in_0({IM_q, multiplexer_3_out[3:1], and_24_out[0]}),
    .in_1({{14{1'b0}}, or_7_out[1], 1'b0}), .out(Imm));
  execPLA execpla_1 (
    .selImm(execpla_1_selimm[0]), .selConst(execpla_1_selimm[1]), .sub(execpla_1_selimm[2]),
    .\logic (execpla_1_selimm[3]), .aPC(execpla_1_selimm[4]), .lowImm(execpla_1_selimm[5]),
    .rd(execpla_1_selimm[6]), .wr(execpla_1_selimm[7]), .we(execpla_1_selimm[8]), .sign(execpla_1_selimm[9]),
    .word(execpla_1_selimm[10]), .selRd(execpla_1_selimm[11]), .slt(execpla_1_selimm[12]));  // open: IR3, IR2, IR1, IR0, imm
  fetchPLA fetchpla_1 (
    .selImm(fetchpla_1_selimm[0]), .selConst(fetchpla_1_selimm[1]), .sub(fetchpla_1_selimm[2]),
    .\logic (fetchpla_1_selimm[3]), .aPC(fetchpla_1_selimm[4]));  // open: reset, cond, alt, JorB, IR0
  Multiplexer #(.Bits(13)) multiplexer_5 (
    .sel(F), .in_0(execpla_1_selimm), .in_1({8'ha, fetchpla_1_selimm}), .out(multiplexer_5_out));

  assign word = logSelect[0];

  // Other names for the same wires on the sheet: IR0 = logSelect[0]; IR1 = logSelect[1]

  // Notes on the sheet:
  //   clock: controls internal registers
  //   reset: when high forces the PC to 0x0000
  //   dIn: data from memory
  //   NE: A ~= B
  //   GE: A >= B
  //   wr: memory write cycle
  //   rd: memory read cycle
  //   sign: not LBU
  //   word: not SB, LB or LBU
  //   sub: change addition to subtraction
  //   logic: select logic operation instead of addition
  //   logSelect: selects between shift right, AND, OR, XOR
  //   Imm: saved from prefix instruction and 4 bits from the current instruction
  //   selImm: B is immediate
  //   Azero: force A to 0
  //   we: updates register Rw
  //   Rw: register to be written
  //   Ra: first register to read
  //   Rb: second register to read
  //   selRd: selects betweenALU result and memory for write back
  //   slt: ignores ALU result and use GE?0x0000:0x0001
endmodule
