// Digital circuit drv16.dig as structural Verilog
// 16 bit processor which is compatible at the assembly language level with RISC-V
module drv16 (
  input  clock,
  input  reset,
  input  [15:0] dIn,
  output [14:0] addr,
  output [15:0] dOut,
  output rd,
  output wrH,
  output wrL
);

  wire ALU_ge, ALU_ne, and_2_out, and_3_out, and_4_out, controlunit_1_azero, controlunit_1_logic,
       controlunit_1_selimm, controlunit_1_selrd, controlunit_1_sign, controlunit_1_slt, controlunit_1_sub,
       controlunit_1_we, controlunit_1_word, controlunit_1_wr;
  wire [0:0] ALU_r, not_1_out;
  wire [1:0] controlunit_1_logselect;
  wire [3:0] controlunit_1_ra, controlunit_1_rb, controlunit_1_rw;
  wire [7:0] multiplexer_1_out, multiplexer_2_out;
  wire [7:7] and_1_out;
  wire [15:0] controlunit_1_imm, multiplexer_3_out, multiplexer_4_out, multiplexer_5_out, multiplexer_6_out,
       registerfile_1_da;
  wire [15:8] registerfile_1_db;

  controlUnit controlunit_1 (
    .clock(clock), .reset(reset), .dIn(dIn), .NE(ALU_ne), .GE(ALU_ge), .wr(controlunit_1_wr), .rd(rd),
    .sign(controlunit_1_sign), .word(controlunit_1_word), .sub(controlunit_1_sub),
    .\logic (controlunit_1_logic), .logSelect(controlunit_1_logselect), .Imm(controlunit_1_imm),
    .selImm(controlunit_1_selimm), .Azero(controlunit_1_azero), .we(controlunit_1_we), .Rw(controlunit_1_rw),
    .Ra(controlunit_1_ra), .Rb(controlunit_1_rb), .selRd(controlunit_1_selrd), .slt(controlunit_1_slt));
  and and_1 (and_1_out[7], multiplexer_1_out[7], controlunit_1_sign);
  Multiplexer #(.Bits(8)) multiplexer_1 (.sel(ALU_r[0]), .in_0(dIn[7:0]), .in_1(dIn[15:8]), .out(multiplexer_1_out));
  Multiplexer #(.Bits(8)) multiplexer_2 (
    .sel(controlunit_1_word), .in_0({8{and_1_out[7]}}), .in_1(dIn[15:8]), .out(multiplexer_2_out));
  not not_1 (not_1_out[0], ALU_ge);
  Multiplexer #(.Bits(16)) multiplexer_3 (
    .sel(controlunit_1_slt), .in_0({addr, ALU_r[0]}), .in_1({{15{1'b0}}, not_1_out[0]}),
    .out(multiplexer_3_out));
  // Probe rS2 on controlunit_1_rb
  // Probe rS1 on controlunit_1_ra
  // Probe rD on controlunit_1_rw
  Multiplexer #(.Bits(16)) multiplexer_4 (
    .sel(controlunit_1_selrd), .in_0(multiplexer_3_out), .in_1({multiplexer_2_out, multiplexer_1_out}),
    .out(multiplexer_4_out));
  // Probe selImm on controlunit_1_selimm
  // Probe we on controlunit_1_we
  // Probe dInBytes on {multiplexer_2_out, multiplexer_1_out}
  RegisterFile #(.AddrBits(4), .Bits(16)) registerfile_1 (
    .Din(multiplexer_4_out), .we(controlunit_1_we), .Rw(controlunit_1_rw), .C(clock), .Ra(controlunit_1_ra),
    .Rb(controlunit_1_rb), .Da(registerfile_1_da), .Db({registerfile_1_db, dOut[7:0]}));
  // Probe dA on registerfile_1_da
  // Probe dB on {registerfile_1_db, dOut[7:0]}
  Multiplexer #(.Bits(16)) multiplexer_5 (
    .sel(controlunit_1_azero), .in_0(registerfile_1_da), .in_1({16{1'b0}}), .out(multiplexer_5_out));
  Multiplexer #(.Bits(16)) multiplexer_6 (
    .sel(controlunit_1_selimm), .in_0({registerfile_1_db, dOut[7:0]}), .in_1(controlunit_1_imm),
    .out(multiplexer_6_out));
  // Probe A on multiplexer_5_out
  alu ALU (
    .R({addr, ALU_r[0]}), .A(multiplexer_5_out), .B(multiplexer_6_out), .sub(controlunit_1_sub),
    .logSelect(controlunit_1_logselect), .\logic (controlunit_1_logic), .NE(ALU_ne), .GE(ALU_ge));
  // Probe B on multiplexer_6_out
  // Probe logSel on controlunit_1_logselect
  // Probe logic on controlunit_1_logic
  and and_2 (and_2_out, ALU_r[0], controlunit_1_wr);
  and and_3 (and_3_out, controlunit_1_word, controlunit_1_wr);
  and and_4 (and_4_out, ~ALU_r[0], controlunit_1_wr);  // And
  Multiplexer #(.Bits(8)) multiplexer_7 (
    .sel(controlunit_1_word), .in_0(dOut[7:0]), .in_1(registerfile_1_db), .out(dOut[15:8]));
  // Probe NE on ALU_ne
  // Probe GE on ALU_ge
  or or_1 (wrH, and_2_out, and_3_out);
  or or_2 (wrL, and_3_out, and_4_out);

  // Notes on the sheet:
  //   addr: selects a 16 bit word in memory to be read or changed
  //   dOut: word to be sent to memory
  //   reset: when high prepares the processor to execute from address 0
  //   dIn: word coming from memory
  //   rd: indicates that memory will be read in this cycle
endmodule
