// Digital circuit execPLA.dig as structural Verilog
// generates control signals for execution cycles (created by Digital from truth table)
module execPLA (
  input  IR3,
  input  IR2,
  input  IR1,
  input  IR0,
  input  imm,
  output selImm,
  output selConst,
  output sub,
  output \logic ,
  output aPC,
  output lowImm,
  output rd,
  output wr,
  output we,
  output sign,
  output word,
  output selRd,
  output slt
);

  wire and_1_out, and_2_out, and_3_out, and_4_out, and_10_out, and_11_out, and_13_out, and_14_out, not_1_out,
       not_2_out, not_3_out, not_4_out;

  not not_1 (not_1_out, IR3);
  not not_2 (not_2_out, IR2);
  not not_3 (not_3_out, IR1);
  not not_4 (not_4_out, IR0);
  and and_1 (and_1_out, not_4_out, not_3_out, not_2_out);
  and and_2 (and_2_out, not_3_out, not_1_out);
  and and_3 (and_3_out, IR2, not_1_out);
  and and_4 (and_4_out, IR3, imm);
  and and_5 (selConst, not_2_out, not_1_out);
  and and_6 (sub, IR1, not_2_out);
  and and_7 (\logic , IR2, IR3);
  and and_8 (aPC, IR0, not_3_out, not_2_out, not_1_out);
  and and_9 (lowImm, IR1, not_1_out);
  and and_10 (and_10_out, not_4_out, not_3_out, not_2_out);
  and and_11 (and_11_out, not_3_out, IR2, not_1_out);
  and and_12 (wr, IR1, IR2, not_1_out);
  or or_1 (we, not_3_out, IR3);
  and and_13 (and_13_out, not_4_out, not_3_out, not_2_out);
  and and_14 (and_14_out, IR2, not_1_out);
  and and_15 (slt, IR0, IR1, not_2_out);
  or or_2 (rd, and_10_out, and_11_out);
  or or_3 (selRd, and_13_out, and_14_out);
  or or_4 (selImm, and_1_out, and_2_out, and_3_out, and_4_out);

  assign sign = IR2;
  assign word = IR0;
endmodule
