// Digital circuit fetchPLA.dig as structural Verilog
// generates control signals during fetch (created by Digital from truth table)
module fetchPLA (
  input  reset,
  input  cond,
  input  alt,
  input  JorB,
  input  IR0,
  output selImm,
  output selConst,
  output sub,
  output \logic ,
  output aPC
);

  wire and_1_out, not_1_out, not_2_out, not_3_out;

  not not_1 (not_1_out, cond);
  not not_2 (not_2_out, alt);
  not not_3 (not_3_out, JorB);
  and and_1 (and_1_out, IR0, not_1_out);
  or or_1 (aPC, IR0, not_3_out, not_2_out);
  or or_2 (selConst, and_1_out, not_3_out, reset);

  assign \logic  = 1'b0;
  assign selImm = 1'b1;
  assign sub = 1'b0;
endmodule
