// Digital circuit r0.dig as structural Verilog
// allows an instruction's register field to be replaced by the PC (register zero) and detects when special handling is needed
module r0 (
  input  [3:0] rin,
  input  pc,
  output [3:0] rout,
  output z
);

  Multiplexer #(.Bits(4)) multiplexer_1 (.sel(pc), .in_0(rin), .in_1(4'b0000), .out(rout));
  and and_1 (z, ~pc, ~rin[0], ~rin[1], ~rin[2], ~rin[3]);  // And

  // Notes on the sheet:
  //   rin: a register field from the instruction
  //   pc: replaced incoming register with 0 (pc)
  //   rout: register field for the rest of the processor
  //   z: indicates that rin was zero and pc was not selected
endmodule
