// Digital circuit regTest.dig as structural Verilog
module regTest (
  input  clock,
  input  [15:0] toRD,
  input  [3:0] rD,
  input  [3:0] rS1,
  input  [3:0] rS2,
  input  we,
  output [15:0] fromRS1,
  output [15:0] fromRS2
);

  RegisterFile #(.AddrBits(4), .Bits(16)) registerfile_1 (
    .Din(toRD), .we(we), .Rw(rD), .C(clock), .Ra(rS1), .Rb(rS2), .Da(fromRS1), .Db(fromRS2));
endmodule
