// Digital circuit system.dig as structural Verilog
// A simple system with a drv16 processor, 64KB of RAM, a terminal and keyboard
module system (
  input  clk
);

  wire and_1_out, and_2_out, comparator_1_eq, cpu_rd, cpu_wrh, cpu_wrl, reset_out;
  wire [7:0] mem0_low_d, mem1_high_d;
  wire [14:0] cpu_addr;
  wire [15:0] cpu_dout, keyboard_1_d, multiplexer_1_out;

  Keyboard keyboard_1 (.C(clk), .en(and_1_out), .D(keyboard_1_d));  // open: av
  DipSwitch reset (.out(reset_out));
  // Probe dIn on multiplexer_1_out
  Multiplexer #(.Bits(16)) multiplexer_1 (
    .sel(comparator_1_eq), .in_0({mem1_high_d, mem0_low_d}), .in_1(keyboard_1_d), .out(multiplexer_1_out));
  drv16 cpu (
    .clock(clk), .reset(reset_out), .dIn(multiplexer_1_out), .addr(cpu_addr), .dOut(cpu_dout), .rd(cpu_rd),
    .wrH(cpu_wrh), .wrL(cpu_wrl));
  and and_1 (and_1_out, cpu_rd, comparator_1_eq);
  // Probe addr on cpu_addr
  Comparator #(.Bits(15)) comparator_1 (.a({15{1'b1}}), .b(cpu_addr), .eq(comparator_1_eq));  // open: gt, lt
  RAMDualPort #(.AddrBits(15), .isProgramMemory("true"), .Bits(8)) mem0_low (
    .A(cpu_addr), .Din(cpu_dout[7:0]), .str(cpu_wrl), .C(clk), .ld(cpu_rd), .D(mem0_low_d));
  RAMDualPort #(.AddrBits(15), .isProgramMemory("true"), .Bits(8)) mem1_high (
    .A(cpu_addr), .Din(cpu_dout[15:8]), .str(cpu_wrh), .C(clk), .ld(cpu_rd), .D(mem1_high_d));
  and and_2 (and_2_out, comparator_1_eq, cpu_wrl);
  Terminal terminal_1 (.D(cpu_dout), .C(clk), .en(and_2_out));

  // Notes on the sheet:
  //   clk: Hz: 10
endmodule
